// Logisim project EntregaFinalLogisim.circ as structural Verilog: 11 circuits, main circuit main
module main (
  input  Jogador,
  input  in_2,
  input  in_3,
  input  in_4,
  input  in_5,
  input  in_6,
  input  in_7,
  input  in_8,
  input  in_9,
  output [3:0] out_10,
  output [3:0] out_11,
  output Maior,
  output Igual,
  output Menor,
  output [3:0] Placar,
  output Acertou,
  output [3:0] Chute_X
);

  wire button_1_out, button_2_out, button_3_out, Chutar_coordenadas_out, comparador_1_p3,
       \negativos_1_negação , \negativos_2_negação ;
  wire [3:0] adder_1_out, ff_4bit_1_saida, ff_4bit_3_p1, multiplexer_1_out, negativos_1_out_2,
       negativos_2_out_2;

  LED led_1 (.in(\negativos_1_negação ));
  Hex_Digit_Display hex_digit_display_1 (.value(negativos_1_out_2));  // open: dp
  Negativos negativos_1 (.in_1({in_2, in_3, in_4, in_5}), .out_2(negativos_1_out_2), .\negação (\negativos_1_negação ));
  Button Chutar_coordenadas (.out(Chutar_coordenadas_out));
  Hex_Digit_Display hex_digit_display_2 (.value(Chute_X));  // open: dp
  Button button_1 (.out(button_1_out));
  Flip_Flop_4bit ff_4bit_1 (.Entrada(Chute_X), .clock(Chutar_coordenadas_out), .saida(ff_4bit_1_saida));  // open: RESET
  Button button_2 (.out(button_2_out));
  Flip_Flop_4bit ff_4bit_2 (.Entrada(multiplexer_1_out), .clock(button_2_out), .saida(Chute_X));  // open: RESET
  // Comparador comparador_1: pin names not known; wires that end beside it: button_1_out, ff_4bit_1_saida, comparador_1_p3, out_10, out_11, Maior, Igual, Menor, Acertou
  // Flip_Flop_4bit ff_4bit_3: pin names not known; wires that end beside it: ff_4bit_3_p1, Chutar_coordenadas_out, comparador_1_p3
  Multiplexer #(.width(4)) multiplexer_1 (
    .in0({in_2, in_3, in_4, in_5}), .in1({in_6, in_7, in_8, in_9}), .out(multiplexer_1_out), .sel(Jogador));  // open: en
  Button button_3 (.out(button_3_out));
  Flip_Flop_4bit ff_4bit_4 (.Entrada(multiplexer_1_out), .clock(button_3_out), .saida(ff_4bit_3_p1));  // open: RESET
  Hex_Digit_Display hex_digit_display_3 (.value(ff_4bit_3_p1));  // open: dp
  Adder #(.width(4)) adder_1 (.a(4'b0001), .b(Placar), .out(adder_1_out));  // open: cin, cout
  Flip_Flop_4bit ff_4bit_5 (.Entrada(adder_1_out), .clock(Acertou), .saida(Placar));  // open: RESET
  Negativos negativos_2 (.in_1({in_6, in_7, in_8, in_9}), .out_2(negativos_2_out_2), .\negação (\negativos_2_negação ));
  Hex_Digit_Display hex_digit_display_4 (.value(Placar));  // open: dp
  LED led_2 (.in(\negativos_2_negação ));
  Hex_Digit_Display hex_digit_display_5 (.value(negativos_2_out_2));  // open: dp

  // Notes on the sheet:
  //   Jogador 0
  //   Chute X
  //   X
  //   Chute Y
  //   Y
  //   Jogador 1
endmodule

module Flip_Flop_4bit (
  input  clock,
  input  [3:0] Entrada,
  input  RESET,
  output [3:0] saida
);

  D_Flip_Flop d_ff_1 (.clk(clock), .D(Entrada[0]), .Q(saida[0]), .reset(RESET));  // open: Qn, preset, en
  D_Flip_Flop d_ff_2 (.clk(clock), .D(Entrada[1]), .Q(saida[1]), .reset(RESET));  // open: Qn, preset, en
  D_Flip_Flop d_ff_3 (.clk(clock), .D(Entrada[2]), .Q(saida[2]), .reset(RESET));  // open: Qn, preset, en
  D_Flip_Flop d_ff_4 (.clk(clock), .D(Entrada[3]), .Q(saida[3]), .reset(RESET));  // open: Qn, preset, en
endmodule

module Comparador (
  input  Start,
  input  [3:0] Entrada_X,
  input  [3:0] Entrada_y,
  input  Neg_X,
  input  Neg_Y,
  output Maior,
  output Igual,
  output Menor,
  output [3:0] ale_x,
  output [3:0] ale_y,
  output Acertou
);

  wire comparator_2_eq, comparator_3_eq, comparator_4_eq, \negativos_1_negação , \negativos_2_negação ;
  wire [3:0] adder_1_out, adder_2_out, multiplexer_1_out, multiplexer_2_out, random_1_out, random_2_out;

  Random #(.width(4)) random_1 (.clk(Start), .out(random_1_out));  // open: next, clr
  Random #(.width(4)) random_2 (.clk(Start), .out(random_2_out));  // open: next, clr
  Adder #(.width(4)) adder_1 (.a(Entrada_X), .b(Entrada_y), .out(adder_1_out));  // open: cin, cout
  Negativos negativos_1 (.in_1(random_1_out), .out_2(ale_x), .\negação (\negativos_1_negação ));
  Negativos negativos_2 (.in_1(random_2_out), .out_2(ale_y), .\negação (\negativos_2_negação ));
  Adder #(.width(4)) adder_2 (.a(ale_x), .b(ale_y), .out(adder_2_out));  // open: cin, cout
  Comparator #(.width(4)) comparator_1 (.a(adder_2_out), .b(adder_1_out), .gt(Maior), .eq(Igual), .lt(Menor));
  Comparator #(.width(1)) comparator_2 (.a(\negativos_1_negação ), .b(Neg_X), .eq(comparator_2_eq));  // open: gt, lt
  Comparator #(.width(1)) comparator_3 (.a(\negativos_2_negação ), .b(Neg_Y), .eq(comparator_3_eq));  // open: gt, lt
  Multiplexer #(.width(4)) multiplexer_1 (
    .in0(4'b1111), .in1(Entrada_y), .out(multiplexer_1_out), .sel(Igual));  // open: en
  Multiplexer #(.width(4)) multiplexer_2 (
    .in0(4'b1101), .in1(ale_y), .out(multiplexer_2_out), .sel(Igual));  // open: en
  Comparator #(.width(4)) comparator_4 (
    .a(multiplexer_1_out), .b(multiplexer_2_out), .eq(comparator_4_eq));  // open: gt, lt
  and and_1 (Acertou, comparator_4_eq, comparator_2_eq, comparator_3_eq);
endmodule

module Negativos (
  input  [3:0] in_1,
  output [3:0] out_2,
  output \negação 
);

  wire [3:0] adder_1_out, not_1_out;

  not not_1 (not_1_out[0], in_1[0]);
  not not_2 (not_1_out[1], in_1[1]);
  not not_3 (not_1_out[2], in_1[2]);
  not not_4 (not_1_out[3], in_1[3]);
  Adder #(.width(4)) adder_1 (.a(not_1_out), .b(4'b0001), .out(adder_1_out));  // open: cin, cout
  Multiplexer #(.width(4)) multiplexer_1 (.in0(in_1), .in1(adder_1_out), .out(out_2), .sel(in_1[3]));  // open: en

  assign \negação  = in_1[3];
endmodule

module JOGO (
  input  in_1,
  input  in_2,
  input  Jogador,
  input  in_4,
  input  in_5,
  input  in_6,
  input  in_7,
  input  in_8,
  input  in_9,
  input  in_10,
  input  in_11,
  output Igual,
  output Menor,
  output Maior,
  output Acertou,
  output [3:0] out_16,
  output [3:0] out_17
);

  wire and_1_out, and_2_out, Chutar_coordenadas_out, Chutar_X_out, Chutar_Y_out, clk, d_ff_1_q, d_ff_2_q,
       demultiplexer_1_out0, demultiplexer_1_out1, DM1, DS1, multiplexer_2_out, \negativos_1_negação ,
       \negativos_2_negação , UM1, undriven, US1;
  wire [3:0] adder_1_out, adder_2_out, ff_4bit_1_saida, ff_4bit_2_saida, ff_4bit_3_saida, ff_4bit_4_saida,
       ff_4bit_5_saida, ff_4bit_6_saida, MDM1, MDM2, MDS1, MDS2, multiplexer_1_out, MUM1, MUM2, MUS1, MUS2,
       negativos_1_out_2, negativos_2_out_2;

  Demultiplexer demultiplexer_1 (
    .out0(demultiplexer_1_out0), .out1(demultiplexer_1_out1), .in(Acertou), .sel(Jogador));  // open: en
  Negativos negativos_1 (.in_1({in_4, in_5, in_6, in_7}), .out_2(negativos_1_out_2), .\negação (\negativos_1_negação ));
  Flip_Flop_4bit ff_4bit_1 (.Entrada(adder_1_out), .clock(demultiplexer_1_out0), .RESET(in_2), .saida(ff_4bit_1_saida));
  Adder #(.width(4)) adder_1 (.a(4'b0001), .b(ff_4bit_1_saida), .out(adder_1_out));  // open: cin, cout
  LED led_1 (.in(\negativos_1_negação ));
  Hex_Digit_Display hex_digit_display_1 (.value(negativos_1_out_2));  // open: dp
  D_Flip_Flop d_ff_1 (.clk(Chutar_X_out), .D(multiplexer_2_out), .Q(d_ff_1_q));  // open: Qn, preset, en, reset
  Hex_Digit_Display hex_digit_display_2 (.value(ff_4bit_1_saida));  // open: dp
  Hex_Digit_Display hex_digit_display_3 (.value(MDM2));  // open: dp
  Button Chutar_X (.out(Chutar_X_out));
  Hex_Digit_Display hex_digit_display_4 (.value(MUM2), .dp(undriven));
  LED led_2 (.in(d_ff_1_q));
  Hex_Digit_Display hex_digit_display_5 (.value(ff_4bit_2_saida));  // open: dp
  Flip_Flop_4bit ff_4bit_2 (.Entrada(multiplexer_1_out), .clock(Chutar_X_out), .saida(ff_4bit_2_saida));  // open: RESET
  Hex_Digit_Display hex_digit_display_6 (.value(MDS2));  // open: dp
  Button Chutar_coordenadas (.out(Chutar_coordenadas_out));
  Flip_Flop_4bit ff_4bit_3 (
    .Entrada(ff_4bit_2_saida), .clock(Chutar_coordenadas_out), .saida(ff_4bit_3_saida));  // open: RESET
  Hex_Digit_Display hex_digit_display_7 (.value(MUS2));  // open: dp
  Button button_1 (.out(UM1));
  Button button_2 (.out(DM1));
  Comparador comparador_1 (
    .Start(Acertou), .Entrada_X(ff_4bit_3_saida), .Entrada_y(ff_4bit_4_saida), .Neg_X(d_ff_1_q),
    .Neg_Y(d_ff_2_q), .Maior(Maior), .Igual(Igual), .Menor(Menor), .ale_x(out_16), .ale_y(out_16),
    .Acertou(Acertou));
  Multiplexer #(.width(4)) multiplexer_1 (
    .in0(negativos_1_out_2), .in1(negativos_2_out_2), .out(multiplexer_1_out), .sel(Jogador));  // open: en
  Multiplexer multiplexer_2 (.in0(in_4), .in1(in_8), .out(multiplexer_2_out), .sel(Jogador));  // open: en
  Button button_3 (.out(DS1));
  LED led_3 (.in(d_ff_2_q));
  Flip_Flop_4bit ff_4bit_4 (
    .Entrada(ff_4bit_5_saida), .clock(Chutar_coordenadas_out), .saida(ff_4bit_4_saida));  // open: RESET
  Hex_Digit_Display hex_digit_display_8 (.value(MDM1));  // open: dp
  Button button_4 (.out(US1));
  Hex_Digit_Display hex_digit_display_9 (.value(ff_4bit_5_saida));  // open: dp
  Hex_Digit_Display hex_digit_display_10 (.value(ff_4bit_6_saida));  // open: dp
  Hex_Digit_Display hex_digit_display_11 (.value(MUM1));  // open: dp
  Button Chutar_Y (.out(Chutar_Y_out));
  Flip_Flop_4bit ff_4bit_5 (.Entrada(multiplexer_1_out), .clock(Chutar_Y_out), .saida(ff_4bit_5_saida));  // open: RESET
  Hex_Digit_Display hex_digit_display_12 (.value(MDS1));  // open: dp
  Hex_Digit_Display hex_digit_display_13 (.value(MUS1));  // open: dp
  LED led_4 (.in(\negativos_2_negação ));
  D_Flip_Flop d_ff_2 (.clk(Chutar_Y_out), .D(multiplexer_2_out), .Q(d_ff_2_q));  // open: Qn, preset, en, reset
  Hex_Digit_Display hex_digit_display_14 (.value(negativos_2_out_2));  // open: dp
  Flip_Flop_4bit ff_4bit_6 (.Entrada(adder_2_out), .clock(demultiplexer_1_out1), .RESET(in_2), .saida(ff_4bit_6_saida));
  Clock clock_1 (.out(clk));
  Adder #(.width(4)) adder_2 (.a(4'b0001), .b(ff_4bit_6_saida), .out(adder_2_out));  // open: cin, cout
  Negativos negativos_2 (
    .in_1({in_8, in_9, in_10, in_11}), .out_2(negativos_2_out_2), .\negação (\negativos_2_negação ));
  TIMER timer_1 (
    .CHAVE(in_1), .RESET(in_2), .DM_2(MDM2), .UM_2(MUM2), .DS_2(MDS2), .US_2(MUS2), .DM(DM1), .UM(UM1),
    .DS(DS1), .US(US1), .CLK(and_1_out));
  and and_1 (and_1_out, Jogador, clk);
  TIMER timer_2 (
    .CHAVE(in_1), .RESET(in_2), .DM_2(MDM1), .UM_2(MUM1), .DS_2(MDS1), .US_2(MUS1), .DM(DM1), .UM(UM1),
    .DS(DS1), .US(US1), .CLK(and_2_out));
  and and_2 (and_2_out, ~Jogador, clk);  // AND_Gate

  assign out_17 = out_16;

  // Other names for the same wires on the sheet: RST = in_2; START = in_1

  // Notes on the sheet:
  //   Jogador 0
  //   X
  //   Y
  //   Jogador 1
endmodule

module CONTADOR_9_0 (
  input  W,
  input  X,
  input  Y,
  input  Z,
  output A,
  output B,
  output C,
  output D
);

  wire and_1_out, and_2_out, and_3_out, and_4_out, and_5_out, and_6_out, and_7_out, and_8_out, and_9_out,
       and_10_out, and_11_out, not_1_out, not_2_out, not_3_out, not_4_out, not_5_out, not_6_out, not_7_out,
       not_8_out, not_9_out, not_10_out;

  not not_1 (not_1_out, W);
  not not_2 (not_2_out, X);
  not not_3 (not_3_out, Y);
  not not_4 (not_4_out, Z);
  and and_1 (and_1_out, X, Z);
  and and_2 (and_2_out, X, Y);
  and and_3 (and_3_out, W, not_5_out, not_6_out);
  not not_5 (not_5_out, Y);
  not not_6 (not_6_out, Z);
  and and_4 (and_4_out, Y, Z);
  and and_5 (and_5_out, X, not_7_out, not_8_out);
  not not_7 (not_7_out, Y);
  not not_8 (not_8_out, Z);
  and and_6 (and_6_out, W, not_9_out, not_10_out);
  not not_9 (not_9_out, Y);
  not not_10 (not_10_out, Z);
  and and_7 (and_7_out, W, X);
  not not_11 (D, Z);
  and and_8 (and_8_out, not_1_out, not_2_out, not_3_out, not_4_out);
  and and_9 (and_9_out, W, Z);
  and and_10 (and_10_out, W, Y);
  and and_11 (and_11_out, W, X);
  or or_1 (B, and_1_out, and_2_out, and_3_out);
  or or_2 (C, and_4_out, and_5_out, and_6_out, and_7_out);
  or or_3 (A, and_8_out, and_9_out, and_10_out, and_11_out);
endmodule

module CONTADOR_5_0 (
  input  X,
  input  Y,
  input  Z,
  output A,
  output B,
  output C
);

  wire and_1_out, and_2_out, and_3_out, and_4_out, and_5_out, not_1_out, not_2_out, not_3_out, not_4_out;

  not not_1 (not_1_out, X);
  not not_2 (not_2_out, Y);
  not not_3 (not_3_out, Z);
  not not_4 (not_4_out, Z);
  not not_5 (C, Z);
  and and_1 (and_1_out, not_1_out, not_2_out, not_3_out);
  and and_2 (and_2_out, X, Z);
  and and_3 (and_3_out, X, Y);
  and and_4 (and_4_out, Y, Z);
  and and_5 (and_5_out, X, not_4_out);
  or or_1 (A, and_1_out, and_2_out, and_3_out);
  or or_2 (B, and_4_out, and_5_out);
endmodule

module UNIDADES (
  input  in_1,
  input  in_2,
  input  in_3,
  input  CHAVE,
  input  RESET,
  input  AJUTE,
  input  in_7,
  output [3:0] out_8,
  output W,
  output X,
  output Y,
  output Z
);

  wire and_1_out, d_ff_1_q, d_ff_2_q, d_ff_3_q, d_ff_4_q, multiplexer_1_out;

  Multiplexer multiplexer_1 (.in0(AJUTE), .in1(and_1_out), .out(multiplexer_1_out), .sel(CHAVE));  // open: en
  and and_1 (and_1_out, in_1, in_2, in_3);
  D_Flip_Flop d_ff_1 (
    .clk(multiplexer_1_out), .D(out_8[0]), .Q(d_ff_1_q), .Qn(Z), .en(in_7), .reset(RESET));  // open: preset
  D_Flip_Flop d_ff_2 (
    .clk(multiplexer_1_out), .D(out_8[1]), .Q(d_ff_2_q), .Qn(Y), .en(in_7), .reset(RESET));  // open: preset
  D_Flip_Flop d_ff_3 (
    .clk(multiplexer_1_out), .D(out_8[2]), .Q(d_ff_3_q), .Qn(X), .en(in_7), .reset(RESET));  // open: preset
  CONTADOR_9_0 contador_9_0_1 (
    .W(d_ff_4_q), .X(d_ff_3_q), .Y(d_ff_2_q), .Z(d_ff_1_q), .A(out_8[3]), .B(out_8[2]), .C(out_8[1]),
    .D(out_8[0]));
  D_Flip_Flop d_ff_4 (
    .clk(multiplexer_1_out), .D(out_8[3]), .Q(d_ff_4_q), .Qn(W), .en(in_7), .reset(RESET));  // open: preset
  Hex_Digit_Display hex_digit_display_1 (.value(out_8));  // open: dp
endmodule

module DEZENAS (
  input  in_1,
  input  in_2,
  input  in_3,
  input  in_4,
  input  CHAVE,
  input  RESET,
  input  BLOQUEIO,
  input  AJUSTE,
  output [3:0] out_9,
  output out_10,
  output out_11,
  output out_12
);

  wire and_1_out, d_ff_1_q, d_ff_2_q, d_ff_3_q, multiplexer_1_out;

  Multiplexer multiplexer_1 (.in0(AJUSTE), .in1(and_1_out), .out(multiplexer_1_out), .sel(CHAVE));  // open: en
  and and_1 (and_1_out, in_1, in_2, in_3, in_4);
  D_Flip_Flop d_ff_1 (
    .clk(multiplexer_1_out), .D(out_9[0]), .Q(d_ff_1_q), .Qn(out_10), .en(BLOQUEIO), .reset(RESET));  // open: preset
  D_Flip_Flop d_ff_2 (
    .clk(multiplexer_1_out), .D(out_9[1]), .Q(d_ff_2_q), .Qn(out_11), .en(BLOQUEIO), .reset(RESET));  // open: preset
  D_Flip_Flop d_ff_3 (
    .clk(multiplexer_1_out), .D(out_9[2]), .Q(d_ff_3_q), .Qn(out_12), .en(BLOQUEIO), .reset(RESET));  // open: preset
  CONTADOR_5_0 contador_5_0_1 (.X(d_ff_3_q), .Y(d_ff_2_q), .Z(d_ff_1_q), .A(out_9[2]), .B(out_9[1]), .C(out_9[0]));
  Hex_Digit_Display hex_digit_display_1 (.value({1'b0, out_9[2:0]}));  // open: dp

  assign out_9[3] = 1'b0;
endmodule

module UNIDADE2_0 (
  input  AJUTE,
  input  CLOCK,
  input  CHAVE,
  input  RESET,
  input  BLOQUEIO,
  output [3:0] out_6,
  output W,
  output X,
  output Y,
  output Z
);

  wire d_ff_1_q, d_ff_2_q, d_ff_3_q, d_ff_4_q, multiplexer_1_out;

  D_Flip_Flop d_ff_1 (
    .clk(multiplexer_1_out), .D(out_6[0]), .Q(d_ff_1_q), .Qn(Z), .en(BLOQUEIO), .reset(RESET));  // open: preset
  Multiplexer multiplexer_1 (.in0(AJUTE), .in1(CLOCK), .out(multiplexer_1_out), .sel(CHAVE));  // open: en
  D_Flip_Flop d_ff_2 (
    .clk(multiplexer_1_out), .D(out_6[1]), .Q(d_ff_2_q), .Qn(Y), .en(BLOQUEIO), .reset(RESET));  // open: preset
  D_Flip_Flop d_ff_3 (
    .clk(multiplexer_1_out), .D(out_6[2]), .Q(d_ff_3_q), .Qn(X), .en(BLOQUEIO), .reset(RESET));  // open: preset
  CONTADOR_9_0 contador_9_0_1 (
    .W(d_ff_4_q), .X(d_ff_3_q), .Y(d_ff_2_q), .Z(d_ff_1_q), .A(out_6[3]), .B(out_6[2]), .C(out_6[1]),
    .D(out_6[0]));
  D_Flip_Flop d_ff_4 (
    .clk(multiplexer_1_out), .D(out_6[3]), .Q(d_ff_4_q), .Qn(W), .en(BLOQUEIO), .reset(RESET));  // open: preset
  Hex_Digit_Display hex_digit_display_1 (.value(out_6));  // open: dp
endmodule

module TIMER (
  input  CHAVE,
  input  RESET,
  input  CLK,
  input  DM,
  input  US,
  input  DS,
  input  UM,
  output [3:0] DM_2,
  output [3:0] UM_2,
  output [3:0] DS_2,
  output [3:0] US_2
);

  wire and_1_out, dezenas_1_out_10, dezenas_1_out_11, dezenas_1_out_12, dezenas_2_out_10, dezenas_2_out_11,
       dezenas_2_out_12, not_1_out, unidade2_0_1_w, unidade2_0_1_x, unidade2_0_1_y, unidade2_0_1_z,
       unidades_1_w, unidades_1_x, unidades_1_y, unidades_1_z;

  Hex_Digit_Display hex_digit_display_1 (.value(DM_2));  // open: dp
  DEZENAS dezenas_1 (
    .in_1(unidades_1_w), .in_2(unidades_1_x), .in_3(unidades_1_y), .in_4(unidades_1_z), .CHAVE(CHAVE),
    .RESET(RESET), .out_9(DM_2), .out_10(dezenas_1_out_10), .out_11(dezenas_1_out_11),
    .out_12(dezenas_1_out_12), .AJUSTE(DM), .BLOQUEIO(not_1_out));
  Hex_Digit_Display hex_digit_display_2 (.value(UM_2));  // open: dp
  UNIDADES unidades_1 (
    .in_1(dezenas_2_out_10), .in_2(dezenas_2_out_11), .in_3(dezenas_2_out_12), .CHAVE(CHAVE), .RESET(RESET),
    .out_8(UM_2), .W(unidades_1_w), .X(unidades_1_x), .Y(unidades_1_y), .Z(unidades_1_z), .AJUTE(UM),
    .in_7(not_1_out));
  and and_1 (and_1_out, unidade2_0_1_w, unidade2_0_1_x, unidade2_0_1_y, ~unidade2_0_1_z, ~dezenas_2_out_10, dezenas_2_out_11, dezenas_2_out_12, unidades_1_w, unidades_1_x, unidades_1_y, ~unidades_1_z, ~dezenas_1_out_10, dezenas_1_out_11, dezenas_1_out_12);  // AND_Gate
  Hex_Digit_Display hex_digit_display_3 (.value(DS_2));  // open: dp
  DEZENAS dezenas_2 (
    .in_1(unidade2_0_1_w), .in_2(unidade2_0_1_x), .in_3(unidade2_0_1_y), .in_4(unidade2_0_1_z),
    .CHAVE(CHAVE), .RESET(RESET), .out_9(DS_2), .out_10(dezenas_2_out_10), .out_11(dezenas_2_out_11),
    .out_12(dezenas_2_out_12), .AJUSTE(DS), .BLOQUEIO(not_1_out));
  not not_1 (not_1_out, and_1_out);
  Hex_Digit_Display hex_digit_display_4 (.value(US_2));  // open: dp
  UNIDADE2_0 unidade2_0_1 (
    .AJUTE(US), .CHAVE(CHAVE), .RESET(RESET), .out_6(US_2), .W(unidade2_0_1_w), .X(unidade2_0_1_x),
    .Y(unidade2_0_1_y), .Z(unidade2_0_1_z), .BLOQUEIO(not_1_out), .CLOCK(CLK));
endmodule
