// Logisim project Projeto_2_circuito.circ as structural Verilog: 5 circuits, main circuit Flip-Flop 4bit
module main (
  input  Jogador,
  input  in_2,
  input  in_3,
  input  in_4,
  input  in_5,
  input  in_6,
  input  in_7,
  input  in_8,
  input  in_9,
  output [3:0] out_10,
  output [3:0] out_11,
  output Maior,
  output Igual,
  output Menor,
  output [3:0] Placar,
  output Acertou,
  output [3:0] Chute_X
);

  wire button_1_out, button_2_out, button_3_out, Chutar_coordenadas_out, \negativos_1_negação ,
       \negativos_2_negação ;
  wire [3:0] adder_1_out, ff_4bit_1_saida, ff_4bit_3_saida, ff_4bit_4_saida, multiplexer_1_out,
       negativos_1_out_2, negativos_2_out_2;

  LED led_1 (.in(\negativos_1_negação ));
  Hex_Digit_Display hex_digit_display_1 (.value(negativos_1_out_2));  // open: dp
  Negativos negativos_1 (.in_1({in_2, in_3, in_4, in_5}), .out_2(negativos_1_out_2), .\negação (\negativos_1_negação ));
  Button Chutar_coordenadas (.out(Chutar_coordenadas_out));
  Hex_Digit_Display hex_digit_display_2 (.value(Chute_X));  // open: dp
  Button button_1 (.out(button_1_out));
  Flip_Flop_4bit ff_4bit_1 (.Entrada(Chute_X), .clock(Chutar_coordenadas_out), .saida(ff_4bit_1_saida));
  Button button_2 (.out(button_2_out));
  Flip_Flop_4bit ff_4bit_2 (.Entrada(multiplexer_1_out), .clock(button_2_out), .saida(Chute_X));
  Comparador comparador_1 (
    .Start(button_1_out), .Entrada_X(ff_4bit_1_saida), .Entrada_y(ff_4bit_3_saida), .x(out_10), .y(out_11),
    .Maior(Maior), .Igual(Igual), .Menor(Menor), .Acertou(Acertou));
  Flip_Flop_4bit ff_4bit_3 (.Entrada(ff_4bit_4_saida), .clock(Chutar_coordenadas_out), .saida(ff_4bit_3_saida));
  Multiplexer #(.width(4)) multiplexer_1 (
    .in0({in_2, in_3, in_4, in_5}), .in1({in_6, in_7, in_8, in_9}), .out(multiplexer_1_out), .sel(Jogador));  // open: en
  Button button_3 (.out(button_3_out));
  Flip_Flop_4bit ff_4bit_4 (.Entrada(multiplexer_1_out), .clock(button_3_out), .saida(ff_4bit_4_saida));
  Hex_Digit_Display hex_digit_display_3 (.value(ff_4bit_4_saida));  // open: dp
  Adder #(.width(4)) adder_1 (.a(4'b0001), .b(Placar), .out(adder_1_out));  // open: cin, cout
  Flip_Flop_4bit ff_4bit_5 (.Entrada(adder_1_out), .clock(Acertou), .saida(Placar));
  Negativos negativos_2 (.in_1({in_6, in_7, in_8, in_9}), .out_2(negativos_2_out_2), .\negação (\negativos_2_negação ));
  Hex_Digit_Display hex_digit_display_4 (.value(Placar));  // open: dp
  LED led_2 (.in(\negativos_2_negação ));
  Hex_Digit_Display hex_digit_display_5 (.value(negativos_2_out_2));  // open: dp

  // Notes on the sheet:
  //   Jogador 0
  //   Chute X
  //   X
  //   Chute Y
  //   Y
  //   Jogador 1
endmodule

module Flip_Flop_4bit (
  input  clock,
  input  [3:0] Entrada,
  output [3:0] saida
);

  D_Flip_Flop d_ff_1 (.clk(clock), .D(Entrada[0]), .Q(saida[0]));  // open: Qn, preset, en, reset
  D_Flip_Flop d_ff_2 (.clk(clock), .D(Entrada[1]), .Q(saida[1]));  // open: Qn, preset, en, reset
  D_Flip_Flop d_ff_3 (.clk(clock), .D(Entrada[2]), .Q(saida[2]));  // open: Qn, preset, en, reset
  D_Flip_Flop d_ff_4 (.clk(clock), .D(Entrada[3]), .Q(saida[3]));  // open: Qn, preset, en, reset
endmodule

module Comparador (
  input  Start,
  input  [3:0] Entrada_X,
  input  [3:0] Entrada_y,
  output [3:0] x,
  output [3:0] y,
  output Maior,
  output Igual,
  output Menor,
  output Acertou
);

  wire [3:0] adder_1_out, adder_2_out, multiplexer_1_out, multiplexer_2_out;

  Random #(.width(4)) random_1 (.clk(Start), .out(x));  // open: next, clr
  Random #(.width(4)) random_2 (.clk(Start), .out(y));  // open: next, clr
  Adder #(.width(4)) adder_1 (.a(x), .b(y), .out(adder_1_out));  // open: cin, cout
  Adder #(.width(4)) adder_2 (.a(Entrada_X), .b(Entrada_y), .out(adder_2_out));  // open: cin, cout
  Comparator #(.width(4)) comparator_1 (.a(adder_1_out), .b(adder_2_out), .gt(Maior), .eq(Igual), .lt(Menor));
  Multiplexer #(.width(4)) multiplexer_1 (
    .in0(4'b1111), .in1(Entrada_y), .out(multiplexer_1_out), .sel(Igual));  // open: en
  Multiplexer #(.width(4)) multiplexer_2 (.in0(4'b1101), .in1(y), .out(multiplexer_2_out), .sel(Igual));  // open: en
  Comparator #(.width(4)) comparator_2 (.a(multiplexer_1_out), .b(multiplexer_2_out), .eq(Acertou));  // open: gt, lt
endmodule

module Negativos (
  input  [3:0] in_1,
  output [3:0] out_2,
  output \negação 
);

  wire [3:0] adder_1_out, not_1_out;

  not not_1 (not_1_out[0], in_1[0]);
  not not_2 (not_1_out[1], in_1[1]);
  not not_3 (not_1_out[2], in_1[2]);
  not not_4 (not_1_out[3], in_1[3]);
  Adder #(.width(4)) adder_1 (.a(not_1_out), .b(4'b0001), .out(adder_1_out));  // open: cin, cout
  Multiplexer #(.width(4)) multiplexer_1 (.in0(in_1), .in1(adder_1_out), .out(out_2), .sel(in_1[3]));  // open: en

  assign \negação  = in_1[3];
endmodule

module JOGO (
  input  Jogador,
  input  in_2,
  input  in_3,
  input  in_4,
  input  in_5,
  input  in_6,
  input  in_7,
  input  in_8,
  input  in_9,
  input  in_10,
  input  in_11,
  input  in_12,
  input  in_13,
  input  in_14,
  input  in_15,
  input  in_16,
  input  in_17,
  output [3:0] out_18,
  output [3:0] out_19,
  output Maior,
  output Igual,
  output Menor,
  output [3:0] Placar,
  output Acertou,
  output [3:0] Chute_X
);

  wire button_1_out, button_2_out, button_3_out, Chutar_coordenadas_out, \negativos_1_negação ,
       \negativos_2_negação , \negativos_3_negação , \negativos_4_negação ;
  wire [3:0] adder_1_out, ff_4bit_1_saida, ff_4bit_3_saida, ff_4bit_4_saida, multiplexer_1_out,
       negativos_1_out_2, negativos_2_out_2, negativos_3_out_2, negativos_4_out_2, undriven, undriven_2;

  LED led_1 (.in(\negativos_2_negação ));
  Hex_Digit_Display hex_digit_display_1 (.value(negativos_2_out_2));  // open: dp
  Negativos negativos_1 (.in_1(undriven), .out_2(negativos_1_out_2), .\negação (\negativos_1_negação ));
  Negativos negativos_2 (.in_1({in_2, in_3, in_4, in_5}), .out_2(negativos_2_out_2), .\negação (\negativos_2_negação ));
  Button Chutar_coordenadas (.out(Chutar_coordenadas_out));
  Hex_Digit_Display hex_digit_display_2 (.value(Chute_X));  // open: dp
  LED led_2 (.in(\negativos_1_negação ));
  Hex_Digit_Display hex_digit_display_3 (.value(negativos_1_out_2));  // open: dp
  Button button_1 (.out(button_1_out));
  Flip_Flop_4bit ff_4bit_1 (.Entrada(Chute_X), .clock(Chutar_coordenadas_out), .saida(ff_4bit_1_saida));
  Button button_2 (.out(button_2_out));
  Flip_Flop_4bit ff_4bit_2 (.Entrada(multiplexer_1_out), .clock(button_2_out), .saida(Chute_X));
  Comparador comparador_1 (
    .Start(button_1_out), .Entrada_X(ff_4bit_1_saida), .Entrada_y(ff_4bit_3_saida), .x(out_18), .y(out_19),
    .Maior(Maior), .Igual(Igual), .Menor(Menor), .Acertou(Acertou));
  Flip_Flop_4bit ff_4bit_3 (.Entrada(undriven_2), .clock(Chutar_coordenadas_out), .saida(ff_4bit_3_saida));
  Multiplexer #(.width(4)) multiplexer_1 (
    .in0({in_2, in_3, in_4, in_5}), .in1({in_6, in_7, in_8, in_9}), .out(multiplexer_1_out), .sel(Jogador));  // open: en
  Button button_3 (.out(button_3_out));
  Flip_Flop_4bit ff_4bit_4 (.Entrada(multiplexer_1_out), .clock(button_3_out), .saida(ff_4bit_4_saida));
  Hex_Digit_Display hex_digit_display_4 (.value(ff_4bit_4_saida));  // open: dp
  Adder #(.width(4)) adder_1 (.a(4'b0001), .b(Placar), .out(adder_1_out));  // open: cin, cout
  Flip_Flop_4bit ff_4bit_5 (.Entrada(adder_1_out), .clock(Acertou), .saida(Placar));
  Hex_Digit_Display hex_digit_display_5 (.value(Placar));  // open: dp
  LED led_3 (.in(\negativos_3_negação ));
  Hex_Digit_Display hex_digit_display_6 (.value(negativos_3_out_2));  // open: dp
  Negativos negativos_3 (.in_1({in_6, in_7, in_8, in_9}), .out_2(negativos_3_out_2), .\negação (\negativos_3_negação ));
  LED led_4 (.in(\negativos_4_negação ));
  Hex_Digit_Display hex_digit_display_7 (.value(negativos_4_out_2));  // open: dp
  Negativos negativos_4 (
    .in_1({in_10, in_11, in_12, in_13}), .out_2(negativos_4_out_2), .\negação (\negativos_4_negação ));

  // Notes on the sheet:
  //   Jogador 0
  //   Chute X
  //   X
  //   Jogador 1
  //   Chute Y
  //   Y
  //   Jogador 1
  //   Jogador 1
endmodule
