// Logisim project Trabalho.circ as structural Verilog
module CONTADOR_6_0 (
  input  X,
  input  Y,
  input  Z,
  output A,
  output B,
  output C
);

  wire and_1_out, and_2_out, and_3_out, and_4_out, and_5_out, and_6_out, and_7_out, not_1_out, not_2_out,
       not_3_out, not_4_out, not_5_out, not_6_out, not_7_out;

  not not_1 (not_1_out, X);
  not not_2 (not_2_out, Y);
  not not_3 (not_3_out, Z);
  not not_4 (not_4_out, Y);
  not not_5 (not_5_out, Z);
  not not_6 (not_6_out, Z);
  not not_7 (not_7_out, Z);
  and and_1 (and_1_out, not_1_out, not_2_out, not_3_out);
  and and_2 (and_2_out, X, Z);
  and and_3 (and_3_out, X, Y);
  and and_4 (and_4_out, not_4_out, not_5_out);
  and and_5 (and_5_out, Y, Z);
  and and_6 (and_6_out, Y, not_6_out);
  and and_7 (and_7_out, X, not_7_out);
  or or_1 (A, and_1_out, and_2_out, and_3_out);
  or or_2 (B, and_4_out, and_5_out);
  or or_3 (C, and_6_out, and_7_out);
endmodule

module CONTADOR_9_0 (
  input  W,
  input  X,
  input  Y,
  input  Z,
  output A,
  output B,
  output C,
  output D
);

  wire and_1_out, and_2_out, and_3_out, and_4_out, and_5_out, and_6_out, and_7_out, and_8_out, and_9_out,
       and_10_out, and_11_out, not_1_out, not_2_out, not_3_out, not_4_out, not_5_out, not_6_out, not_7_out,
       not_8_out, not_9_out, not_10_out;

  not not_1 (not_1_out, W);
  not not_2 (not_2_out, X);
  not not_3 (not_3_out, Y);
  not not_4 (not_4_out, Z);
  and and_1 (and_1_out, X, Z);
  and and_2 (and_2_out, X, Y);
  not not_5 (not_5_out, Y);
  and and_3 (and_3_out, W, not_5_out, not_6_out);
  not not_6 (not_6_out, Z);
  and and_4 (and_4_out, Y, Z);
  and and_5 (and_5_out, X, not_7_out, not_8_out);
  not not_7 (not_7_out, Y);
  not not_8 (not_8_out, Z);
  and and_6 (and_6_out, W, not_9_out, not_10_out);
  not not_9 (not_9_out, Y);
  not not_10 (not_10_out, Z);
  and and_7 (and_7_out, W, X);
  not not_11 (D, Z);
  and and_8 (and_8_out, not_1_out, not_2_out, not_3_out, not_4_out);
  and and_9 (and_9_out, W, Z);
  and and_10 (and_10_out, W, Y);
  and and_11 (and_11_out, W, X);
  or or_1 (B, and_1_out, and_2_out, and_3_out);
  or or_2 (C, and_4_out, and_5_out, and_6_out, and_7_out);
  or or_3 (A, and_8_out, and_9_out, and_10_out, and_11_out);
endmodule

module TEMPO (
  input  in_1,
  input  in_2,
  input  in_3,
  input  CHAVE,
  input  RESET,
  input  AJUTE,
  input  in_7,
  output [3:0] out_8,
  output W,
  output X,
  output Y,
  output Z
);

  wire and_1_out, d_ff_1_q, d_ff_2_q, d_ff_3_q, d_ff_4_q, multiplexer_1_out;

  Multiplexer multiplexer_1 (.in0(AJUTE), .in1(and_1_out), .out(multiplexer_1_out), .sel(CHAVE));  // open: en
  and and_1 (and_1_out, in_1, in_2, in_3);
  D_Flip_Flop d_ff_1 (
    .clk(multiplexer_1_out), .D(out_8[0]), .Q(d_ff_1_q), .Qn(Z), .en(in_7), .reset(RESET));  // open: preset
  D_Flip_Flop d_ff_2 (
    .clk(multiplexer_1_out), .D(out_8[1]), .Q(d_ff_2_q), .Qn(Y), .en(in_7), .reset(RESET));  // open: preset
  D_Flip_Flop d_ff_3 (
    .clk(multiplexer_1_out), .D(out_8[2]), .Q(d_ff_3_q), .Qn(X), .en(in_7), .reset(RESET));  // open: preset
  CONTADOR_9_0 contador_9_0_1 (
    .W(d_ff_4_q), .X(d_ff_3_q), .Y(d_ff_2_q), .Z(d_ff_1_q), .A(out_8[3]), .B(out_8[2]), .C(out_8[1]),
    .D(out_8[0]));
  D_Flip_Flop d_ff_4 (
    .clk(multiplexer_1_out), .D(out_8[3]), .Q(d_ff_4_q), .Qn(W), .en(in_7), .reset(RESET));  // open: preset
  Hex_Digit_Display hex_digit_display_1 (.value(out_8));  // open: dp
endmodule

module DEZENAS (
  input  in_1,
  input  in_2,
  input  in_3,
  input  in_4,
  input  CHAVE,
  input  RESET,
  input  BLOQUEIO,
  input  AJUSTE,
  output [3:0] out_9,
  output out_10,
  output out_11,
  output out_12
);

  wire and_1_out, d_ff_1_q, d_ff_2_q, d_ff_3_q, multiplexer_1_out;

  Multiplexer multiplexer_1 (.in0(AJUSTE), .in1(and_1_out), .out(multiplexer_1_out), .sel(CHAVE));  // open: en
  and and_1 (and_1_out, in_1, in_2, in_3, in_4);
  D_Flip_Flop d_ff_1 (
    .clk(multiplexer_1_out), .D(out_9[0]), .Q(d_ff_1_q), .Qn(out_10), .en(BLOQUEIO), .reset(RESET));  // open: preset
  D_Flip_Flop d_ff_2 (
    .clk(multiplexer_1_out), .D(out_9[1]), .Q(d_ff_2_q), .Qn(out_11), .en(BLOQUEIO), .reset(RESET));  // open: preset
  D_Flip_Flop d_ff_3 (
    .clk(multiplexer_1_out), .D(out_9[2]), .Q(d_ff_3_q), .Qn(out_12), .en(BLOQUEIO), .reset(RESET));  // open: preset
  CONTADOR_5_0 contador_5_0_1 (.X(d_ff_3_q), .Y(d_ff_2_q), .Z(d_ff_1_q), .A(out_9[2]), .B(out_9[1]), .C(out_9[0]));
  Hex_Digit_Display hex_digit_display_1 (.value({1'b0, out_9[2:0]}));  // open: dp

  assign out_9[3] = 1'b0;
endmodule

module TALVEZ_SEGUNDOS (
  input  in_1,
  input  AJUSTE_US,
  input  in_3
);

  wire and_1_out, dezenas_1_out_10, dezenas_1_out_11, dezenas_1_out_12, dezenas_2_p7, dezenas_2_p8,
       not_1_out, not_2_out, segundos_1_p7, tempo_1_p1, tempo_1_p2, tempo_1_p3, tempo_1_p5, tempo_1_p7,
       tempo_1_p8, tempo_1_p9;
  wire [3:0] dezenas_1_out_9, dezenas_2_p4, segundos_1_p4, tempo_1_p4;

  Hex_Digit_Display hex_digit_display_1 (.value(dezenas_1_out_9));  // open: dp
  DEZENAS dezenas_1 (
    .in_1(tempo_1_p3), .in_2(tempo_1_p3), .in_4(tempo_1_p2), .out_9(dezenas_1_out_9),
    .out_10(dezenas_1_out_10), .out_11(dezenas_1_out_11), .out_12(dezenas_1_out_12), .BLOQUEIO(tempo_1_p5),
    .RESET(tempo_1_p1), .CHAVE(in_1));  // open: in_3, AJUSTE
  Hex_Digit_Display hex_digit_display_2 (.value(tempo_1_p4));  // open: dp
  // TEMPO tempo_1: pin names not known; wires that end beside it: tempo_1_p1, tempo_1_p2, tempo_1_p3, tempo_1_p4, tempo_1_p5, in_1, tempo_1_p7, tempo_1_p8, tempo_1_p9
  Hex_Digit_Display hex_digit_display_3 (.value(dezenas_2_p4));  // open: dp
  // DEZENAS dezenas_2: pin names not known; wires that end beside it: tempo_1_p7, tempo_1_p8, tempo_1_p9, dezenas_2_p4, tempo_1_p5, in_1, dezenas_2_p7, dezenas_2_p8, tempo_1_p5
  not not_1 (not_1_out, dezenas_1_out_10);
  Hex_Digit_Display hex_digit_display_4 (.value(segundos_1_p4));  // open: dp
  not not_2 (not_2_out, tempo_1_p1);
  // SEGUNDOS segundos_1: pin names not known; wires that end beside it: dezenas_2_p7, dezenas_2_p8, tempo_1_p5, segundos_1_p4, tempo_1_p5, in_3, segundos_1_p7, in_1, AJUSTE_US
  and and_1 (and_1_out, ~in_1, dezenas_2_p7, dezenas_2_p8, tempo_1_p5, tempo_1_p7, tempo_1_p8, ~tempo_1_p9, ~not_2_out, tempo_1_p2, tempo_1_p3, tempo_1_p3, ~not_1_out, dezenas_1_out_11, dezenas_1_out_12);  // AND_Gate
  not not_3 (tempo_1_p5, and_1_out);
  Clock clock_1 (.out(segundos_1_p7));
endmodule

module CONTADOR_5_0 (
  input  X,
  input  Y,
  input  Z,
  output A,
  output B,
  output C
);

  wire and_1_out, and_2_out, and_3_out, and_4_out, and_5_out, not_1_out, not_2_out, not_3_out, not_4_out;

  not not_1 (not_1_out, X);
  not not_2 (not_2_out, Y);
  not not_3 (not_3_out, Z);
  not not_4 (not_4_out, Z);
  not not_5 (C, Z);
  and and_1 (and_1_out, not_1_out, not_2_out, not_3_out);
  and and_2 (and_2_out, X, Z);
  and and_3 (and_3_out, X, Y);
  and and_4 (and_4_out, Y, Z);
  and and_5 (and_5_out, X, not_4_out);
  or or_1 (A, and_1_out, and_2_out, and_3_out);
  or or_2 (B, and_4_out, and_5_out);
endmodule

module SEGUNDOS (
  input  AJUTE,
  input  CLOCK,
  input  CHAVE,
  input  RESET,
  input  BLOQUEIO,
  output [3:0] out_6,
  output W,
  output X,
  output Y,
  output Z
);

  wire d_ff_1_q, d_ff_2_q, d_ff_3_q, d_ff_4_q, multiplexer_1_out;

  Multiplexer multiplexer_1 (.in0(AJUTE), .in1(CLOCK), .out(multiplexer_1_out), .sel(CHAVE));  // open: en
  D_Flip_Flop d_ff_1 (
    .clk(multiplexer_1_out), .D(out_6[0]), .Q(d_ff_1_q), .Qn(Z), .en(BLOQUEIO), .reset(RESET));  // open: preset
  D_Flip_Flop d_ff_2 (
    .clk(multiplexer_1_out), .D(out_6[1]), .Q(d_ff_2_q), .Qn(Y), .en(BLOQUEIO), .reset(RESET));  // open: preset
  D_Flip_Flop d_ff_3 (
    .clk(multiplexer_1_out), .D(out_6[2]), .Q(d_ff_3_q), .Qn(X), .en(BLOQUEIO), .reset(RESET));  // open: preset
  CONTADOR_9_0 contador_9_0_1 (
    .W(d_ff_4_q), .X(d_ff_3_q), .Y(d_ff_2_q), .Z(d_ff_1_q), .A(out_6[3]), .B(out_6[2]), .C(out_6[1]),
    .D(out_6[0]));
  D_Flip_Flop d_ff_4 (
    .clk(multiplexer_1_out), .D(out_6[3]), .Q(d_ff_4_q), .Qn(W), .en(BLOQUEIO), .reset(RESET));  // open: preset
  Hex_Digit_Display hex_digit_display_1 (.value(out_6));  // open: dp
endmodule

module TIMER (
  input  CHAVE,
  input  RESET,
  input  AJUSTE_DM,
  input  AJUSTE_UM,
  input  AJUSTE_DS,
  input  AJUSTE_US
);

  wire and_1_out, clock_1_out, dezenas_1_out_10, dezenas_1_out_11, dezenas_1_out_12, dezenas_2_out_10,
       dezenas_2_out_11, dezenas_2_out_12, not_1_out, segundos_1_w, segundos_1_x, segundos_1_y, segundos_1_z,
       tempo_1_w, tempo_1_x, tempo_1_y, tempo_1_z;
  wire [3:0] dezenas_1_out_9, dezenas_2_out_9, segundos_1_out_6, tempo_1_out_8;

  Hex_Digit_Display hex_digit_display_1 (.value(dezenas_1_out_9));  // open: dp
  DEZENAS dezenas_1 (
    .in_1(tempo_1_w), .in_2(tempo_1_x), .in_3(tempo_1_y), .in_4(tempo_1_z), .out_9(dezenas_1_out_9),
    .out_10(dezenas_1_out_10), .out_11(dezenas_1_out_11), .out_12(dezenas_1_out_12), .BLOQUEIO(not_1_out),
    .RESET(RESET), .AJUSTE(AJUSTE_DM), .CHAVE(CHAVE));
  Hex_Digit_Display hex_digit_display_2 (.value(tempo_1_out_8));  // open: dp
  TEMPO tempo_1 (
    .in_1(dezenas_2_out_10), .in_3(dezenas_2_out_12), .RESET(RESET), .out_8(tempo_1_out_8), .W(tempo_1_w),
    .X(tempo_1_x), .Y(tempo_1_y), .Z(tempo_1_z), .in_7(not_1_out), .AJUTE(AJUSTE_UM),
    .in_2(dezenas_2_out_11), .CHAVE(CHAVE));
  Hex_Digit_Display hex_digit_display_3 (.value(dezenas_2_out_9));  // open: dp
  DEZENAS dezenas_2 (
    .in_1(segundos_1_w), .in_2(segundos_1_x), .in_3(segundos_1_y), .in_4(segundos_1_z),
    .out_9(dezenas_2_out_9), .out_10(dezenas_2_out_10), .out_11(dezenas_2_out_11), .out_12(dezenas_2_out_12),
    .BLOQUEIO(not_1_out), .RESET(RESET), .AJUSTE(AJUSTE_DS), .CHAVE(CHAVE));
  and and_1 (and_1_out, ~segundos_1_z, segundos_1_y, segundos_1_x, segundos_1_w, ~dezenas_2_out_10, dezenas_2_out_11, dezenas_2_out_12, tempo_1_w, tempo_1_x, tempo_1_y, ~tempo_1_z, ~dezenas_1_out_10, dezenas_1_out_11, dezenas_1_out_12);  // AND_Gate
  not not_1 (not_1_out, and_1_out);
  Hex_Digit_Display hex_digit_display_4 (.value(segundos_1_out_6));  // open: dp
  SEGUNDOS segundos_1 (
    .AJUTE(AJUSTE_US), .RESET(RESET), .out_6(segundos_1_out_6), .W(segundos_1_w), .X(segundos_1_x),
    .Y(segundos_1_y), .Z(segundos_1_z), .BLOQUEIO(not_1_out), .CLOCK(clock_1_out), .CHAVE(CHAVE));
  Clock clock_1 (.out(clock_1_out));
endmodule
